# Fritzing sketch Sketch2Basico (saved by Fritzing 0.9.9b)
breadboards: 1

parts:
  U1 = ESP8266 NodeMCU LoLin module
  L298N1 = L298N DC motor driver
  VCC1 = Battery block 9V  # not connected
  M2 = DC Motor  # not connected
  M3 = DC Motor  # not connected
  BT1 = Bluetooth HC-06u [package=THT]
  Power_plug1 = USB-C plug  # not connected

nets:
  N1: U1.D0, L298N1.ENA
  N2: U1.D1, L298N1.IN1
  N3: U1.D2, L298N1.IN2
  N4: U1.D3, L298N1.IN3
  N5: U1.D4, L298N1.IN4
  3V3: U1.3V3, BT1.VCC
  N6: U1.D5, L298N1.ENB
  N7: U1.D7, BT1.TXD
  N8: U1.D8, BT1.RXD
  GND: U1.GND, BT1.GND

custom parts:
  ESP8266 NodeMCU LoLin module: ESP8266 based NodeMCU
  L298N DC motor driver: 2x DC motor driver with 78M05 positive voltage regulator (7..35 V) L298N: max 46 V, 2 A Set 5 V Enable jumper to enable 5 V regultor (needed for the L298N) and +5 V output at screw terminal or supply external +5 V at screw terminal Set ENA and/or ENB to +5 V to enable motor permanently or supply ENA and/or ENB with PWM signal IN1 and IN2 set rotation directory for motor A (OUT1/OUT2) IN2 and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
  Bluetooth HC-06u: Bluetooth HC-06 - face up, pins down 16.5mm x 37.5mm PCB
  USB-C plug: power plug
